# Fritzing sketch 1led curcuit (saved by Fritzing 0.9.2b)
breadboards: 1

parts:
  J1 = T Cobbler Plus  # not connected
  BATT1 = 4xAA Switchable Battery Pack w/Bare Wire
  LED5 = LED - 5mm [color="Red (633nm)" package="5 mm [THT]"]
  R1 = Resistor [tolerance=±5% resistance=270 package=THT]

nets:
  N1: BATT1.POS, LED5.anode
  N2: BATT1.NEG, R1.Pin_1
  N3: LED5.cathode, R1.Pin_0

custom parts:
  T Cobbler Plus: The T-Cobbler Plus is an add on prototyping board from Adafruit specifically designed for the Raspberry Pi B+ that can break out all those tasty power, GPIO, I2C and SPI pins from the 40-pin header onto a solderless breadboard. This set will make "cobbling together" prototypes with the Pi super easy. The T-Cobbler Plus can plug into any solderless breadboard.
  4xAA Switchable Battery Pack w/Bare Wire: 4xAA Switchable Battery Pack with Bare Wire connection
