# Fritzing sketch 1resistor_curcuit (saved by Fritzing 0.9.2b)

parts:
  V1 = DC Power [voltage=6V]
  R1 = Resistor [tolerance=±5% resistance=270 package=THT]
  R1_2 = Resistor [tolerance=±5% resistance=270 package=THT]

nets:
  N1: V1.V+, R1.Pin_0, R1_2.Pin_0
  N2: V1.V-, R1.Pin_1, R1_2.Pin_1
