# Fritzing sketch 3led-parallel (saved by Fritzing 0.9.2b)
breadboards: 1

parts:
  J1 = T Cobbler Plus  # not connected
  BATT1 = 4xAA Switchable Battery Pack w/Bare Wire
  R1 = Resistor [tolerance=±5% resistance=270 package=THT]
  LED4 = LED - 5mm [color="Red (633nm)" package="5 mm [THT]"]
  LED5 = LED - 5mm [color="Red (633nm)" package="5 mm [THT]"]
  LED6 = LED - 5mm [color="Red (633nm)" package="5 mm [THT]"]

nets:
  N1: BATT1.POS, LED4.anode, LED5.anode, LED6.anode
  N2: BATT1.NEG, R1.Pin_0
  N3: R1.Pin_1, LED4.cathode, LED5.cathode, LED6.cathode

custom parts:
  T Cobbler Plus: The T-Cobbler Plus is an add on prototyping board from Adafruit specifically designed for the Raspberry Pi B+ that can break out all those tasty power, GPIO, I2C and SPI pins from the 40-pin header onto a solderless breadboard. This set will make "cobbling together" prototypes with the Pi super easy. The T-Cobbler Plus can plug into any solderless breadboard.
  4xAA Switchable Battery Pack w/Bare Wire: 4xAA Switchable Battery Pack with Bare Wire connection
