# Fritzing sketch 3led-series_no_bread (saved by Fritzing 0.9.2b)
breadboards: 1

parts:
  J1 = T Cobbler Plus  # not connected
  BATT1 = 4xAA Switchable Battery Pack w/Bare Wire
  LED1 = LED - 5mm [color="Red (633nm)" package="5 mm [THT]"]
  LED2 = LED - 5mm [color="Red (633nm)" package="5 mm [THT]"]
  LED3 = LED - 5mm [color="Red (633nm)" package="5 mm [THT]"]
  R1 = Resistor [tolerance=±5% resistance=270 package=THT]

nets:
  N1: BATT1.POS, LED1.anode
  N2: BATT1.NEG, R1.Pin_0
  N3: LED1.cathode, LED2.anode
  N4: LED2.cathode, LED3.anode
  N5: LED3.cathode, R1.Pin_1

custom parts:
  T Cobbler Plus: The T-Cobbler Plus is an add on prototyping board from Adafruit specifically designed for the Raspberry Pi B+ that can break out all those tasty power, GPIO, I2C and SPI pins from the 40-pin header onto a solderless breadboard. This set will make "cobbling together" prototypes with the Pi super easy. The T-Cobbler Plus can plug into any solderless breadboard.
  4xAA Switchable Battery Pack w/Bare Wire: 4xAA Switchable Battery Pack with Bare Wire connection
