# Fritzing sketch 3led (saved by Fritzing 0.9.2b)
breadboards: 1

parts:
  J1 = T Cobbler Plus
  LED1 = LED - 5mm [color="Red (633nm)" package="5 mm [THT]"]
  R1 = Resistor [tolerance=±5% resistance=220 package=THT]
  LED3 = LED - 5mm [color="Green (565nm)" package="5 mm [THT]"]
  R2 = Resistor [tolerance=±5% resistance=220 package=THT]
  R3 = Resistor [tolerance=±5% resistance=220 package=THT]
  VCC2 = Battery  # not connected
  BATT1 = 4xAA Switchable Battery Pack w/Bare Wire
  BAT1 = Battery Holders [package=battery-aa-panel]  # not connected

nets:
  N1: J1.#17, LED1.anode
  N2: J1.#22, LED3.anode
  N3: J1.GND#19, R1.Pin_0, R2.Pin_0, R3.Pin_0, BATT1.NEG
  N4: LED1.cathode, R1.Pin_1
  N5: LED3.cathode, R3.Pin_1

custom parts:
  T Cobbler Plus: The T-Cobbler Plus is an add on prototyping board from Adafruit specifically designed for the Raspberry Pi B+ that can break out all those tasty power, GPIO, I2C and SPI pins from the 40-pin header onto a solderless breadboard. This set will make "cobbling together" prototypes with the Pi super easy. The T-Cobbler Plus can plug into any solderless breadboard.
  4xAA Switchable Battery Pack w/Bare Wire: 4xAA Switchable Battery Pack with Bare Wire connection
