# Fritzing sketch 3led_parallel_schematic (saved by Fritzing 0.9.2b)

parts:
  LED1 = LED - 5mm [color="Red (633nm)" package="5 mm [THT]"]
  LED2 = LED - 5mm [color="Red (633nm)" package="5 mm [THT]"]
  R1 = Resistor [tolerance=±5% resistance=270 package=THT]
  V1 = DC Power [voltage=6V]
  LED3 = LED - 5mm [color="Red (633nm)" package="5 mm [THT]"]

nets:
  N1: LED1.cathode, LED2.cathode, R1.Pin_0, LED3.cathode
  N2: LED1.anode, LED2.anode, V1.V+, LED3.anode
  N3: R1.Pin_1, V1.V-
