# Fritzing sketch 3led_series_schematic (saved by Fritzing 0.9.2b)

parts:
  LED1 = LED - 5mm [color="Red (633nm)" package="5 mm [THT]"]
  LED2 = LED - 5mm [color="Red (633nm)" package="5 mm [THT]"]
  LED3 = LED - 5mm [color="Red (633nm)" package="5 mm [THT]"]
  R1 = Resistor [tolerance=±5% resistance=270 package=THT]
  V1 = DC Power [voltage=6V]

nets:
  N1: LED1.cathode, LED2.anode
  N2: LED1.anode, V1.V+
  N3: LED2.cathode, LED3.anode
  N4: LED3.cathode, R1.Pin_0
  N5: R1.Pin_1, V1.V-
