# Fritzing sketch AND-curcuit (saved by Fritzing 0.9.2b)
breadboards: 1

parts:
  R1 = Resistor [tolerance=±5% resistance=330 package=THT]
  Q1 = NPN-Transistor [package="TO92 [THT]"]
  Q2 = NPN-Transistor [package="TO92 [THT]"]
  R2 = Resistor [tolerance=±5% resistance=330 package=THT]
  VCC1 = Battery
  R3 = Resistor [tolerance=±5% resistance=330 package=THT]
  VCC2 = Battery
  LED1 = LED - 5mm [color="Red (633nm)" package="5 mm [THT]"]

nets:
  N1: R1.Pin_0, R2.Pin_0, VCC2.+
  N2: R1.Pin_1, Q1.B
  N3: Q1.E, Q2.C
  N4: Q1.C, VCC1.-, R3.Pin_0, VCC2.-, LED1.cathode
  N5: Q2.E, R3.Pin_1, LED1.anode
  N6: Q2.B, R2.Pin_1
