# Fritzing sketch RPiConnectorForPiTop-02 (saved by Fritzing 0.9.2b)
circuit board: 9cm x 6.5cm
breadboards: 1

parts:
  J5 = double row female pin header, 14 pins [form="♀ (female)"]  # not connected
  J1 = double row female pin header, 40 pins [form="♀ (female)"]
  J2 = double row female pin header, 40 pins [form="♀ (female)"]
  J6 = double row female pin header, 14 pins [form="♀ (female)"]
  J7 = double row female pin header, 26 pins [form="♀ (female)"]
  J8 = double row female pin header, 14 pins [form="♀ (female)"]
  J9 = double row female pin header, 26 pins [form="♀ (female)"]
  Raspberry_Pi1 = Raspberry Pi 2  # not connected

nets:
  N1: J1.pin1, J2.pin1
  N2: J1.pin2, J2.pin2
  N3: J1.pin3, J2.pin3
  N4: J1.pin4, J2.pin4
  N5: J1.pin5, J2.pin5
  N6: J1.pin6, J2.pin6
  N7: J1.pin7, J2.pin7
  N8: J1.pin8, J2.pin8
  N9: J1.pin9, J2.pin9
  N10: J1.pin10, J2.pin10
  N11: J1.pin11, J2.pin11
  N12: J1.pin12, J2.pin12
  N13: J1.pin13, J2.pin13
  N14: J1.pin14, J2.pin14
  N15: J1.pin15, J2.pin15
  N16: J1.pin16, J2.pin16
  N17: J1.pin17, J2.pin17
  N18: J1.pin18, J2.pin18
  N19: J1.pin19, J2.pin19
  N20: J1.pin20, J2.pin20
  N21: J2.pin21, J6.pin8, J8.pin8
  N22: J2.pin22, J6.pin9, J8.pin9
  N23: J2.pin23, J6.pin10, J8.pin10
  N24: J2.pin24, J6.pin11, J8.pin11
  N25: J2.pin25, J6.pin12, J8.pin12
  N26: J2.pin26, J6.pin13, J8.pin13
  N27: J2.pin27, J6.pin14, J8.pin14
  N28: J2.pin28, J7.pin14, J9.pin14
  N29: J2.pin29, J7.pin15, J9.pin15
  N30: J2.pin30, J7.pin16, J9.pin16
  N31: J2.pin31, J7.pin17, J9.pin17
  N32: J2.pin32, J7.pin18, J9.pin18
  N33: J2.pin33, J7.pin19, J9.pin19
  N34: J2.pin34, J7.pin20, J9.pin20
  N35: J2.pin35, J7.pin21, J9.pin21
  N36: J2.pin36, J7.pin22, J9.pin22
  N37: J2.pin37, J7.pin23, J9.pin23
  N38: J2.pin38, J7.pin24, J9.pin24
  N39: J2.pin39, J7.pin25, J9.pin25
  N40: J2.pin40, J7.pin26, J9.pin26
