# Fritzing sketch RPiConnectorForPiTop-03 (saved by Fritzing 0.9.2b)
circuit board: 9.5cm x 5.7cm
breadboards: 1

parts:
  J5 = double row female pin header, 14 pins [form="♀ (female)"]
  J7 = double row female pin header, 26 pins [form="♀ (female)"]
  J8 = double row female pin header, 40 pins [form="♀ (female)"]
  J2 = double row female pin header, 40 pins [form="♀ (female)"]
  J1 = double row female pin header, 40 pins [form="♀ (female)"]

nets:
  N1: J5.pin1, J8.pin14, J2.pin14, J1.pin14
  N2: J5.pin2, J8.pin15, J2.pin15, J1.pin15
  N3: J5.pin3, J8.pin16, J2.pin16, J1.pin16
  N4: J5.pin4, J8.pin17, J2.pin17, J1.pin17
  N5: J5.pin5, J8.pin18, J2.pin18, J1.pin18
  N6: J5.pin6, J8.pin19, J2.pin19, J1.pin19
  N7: J5.pin7, J8.pin20, J2.pin20, J1.pin20
  N8: J5.pin8, J8.pin21, J2.pin21
  N9: J5.pin9, J2.pin22
  N10: J5.pin10, J2.pin23
  N11: J5.pin11, J2.pin24
  N12: J5.pin12, J2.pin25
  N13: J5.pin13, J2.pin26
  N14: J5.pin14, J2.pin27
  N15: J7.pin1, J8.pin1, J2.pin1, J1.pin1
  N16: J7.pin2, J8.pin2, J2.pin2, J1.pin2
  N17: J7.pin3, J8.pin3, J2.pin3, J1.pin3
  N18: J7.pin4, J8.pin4, J2.pin4, J1.pin4
  N19: J7.pin5, J8.pin5, J2.pin5, J1.pin5
  N20: J7.pin6, J8.pin6, J2.pin6, J1.pin6
  N21: J7.pin7, J8.pin7, J2.pin7, J1.pin7
  N22: J7.pin8, J8.pin8, J2.pin8, J1.pin8
  N23: J7.pin9, J8.pin9, J2.pin9, J1.pin9
  N24: J7.pin10, J8.pin10, J2.pin10, J1.pin10
  N25: J7.pin11, J8.pin11, J2.pin11, J1.pin11
  N26: J7.pin12, J8.pin12, J2.pin12, J1.pin12
  N27: J7.pin13, J8.pin13, J2.pin13, J1.pin13
  N28: J7.pin14, J2.pin28
  N29: J7.pin15, J2.pin29
  N30: J7.pin16, J2.pin30
  N31: J7.pin17, J2.pin31
  N32: J7.pin18, J2.pin32
  N33: J7.pin19, J2.pin33
  N34: J7.pin20, J2.pin34
  N35: J7.pin21, J2.pin35
  N36: J7.pin22, J2.pin36
  N37: J7.pin23, J2.pin37
  N38: J7.pin24, J8.pin38, J2.pin38
  N39: J7.pin25, J8.pin39, J2.pin39
  N40: J7.pin26, J8.pin40, J2.pin40, J1.pin40
