# Fritzing sketch RPiConnectorForPiTop (saved by Fritzing 0.9.2b)
circuit board: 8.5cm x 5.8cm
breadboards: 1

parts:
  J1 = double row female pin header, 40 pins [form="♀ (female)"]
  J2 = double row female pin header, 40 pins [form="♀ (female)"]
  J4 = double row female pin header, 26 pins [form="♀ (female)"]
  J5 = double row female pin header, 14 pins [form="♀ (female)"]

nets:
  N1: J1.pin1, J2.pin1, J4.pin1
  N2: J1.pin2, J2.pin2, J4.pin2
  N3: J1.pin3, J2.pin3, J4.pin3
  N4: J1.pin4, J2.pin4, J4.pin4
  N5: J1.pin5, J2.pin5, J4.pin5
  N6: J1.pin6, J2.pin6, J4.pin6
  N7: J1.pin7, J2.pin7, J4.pin7
  N8: J1.pin8, J2.pin8, J4.pin8
  N9: J1.pin9, J2.pin9, J4.pin9
  N10: J1.pin10, J2.pin10, J4.pin10
  N11: J1.pin11, J2.pin11, J4.pin11
  N12: J1.pin12, J2.pin12, J4.pin12
  N13: J1.pin13, J2.pin13, J4.pin13
  N14: J1.pin14, J2.pin14, J5.pin1
  N15: J1.pin15, J2.pin15, J5.pin2
  N16: J1.pin16, J2.pin16, J5.pin3
  N17: J1.pin17, J2.pin17, J5.pin4
  N18: J1.pin18, J2.pin18, J5.pin5
  N19: J1.pin19, J2.pin19, J5.pin6
  N20: J1.pin20, J2.pin20, J5.pin7
  N21: J1.pin21, J2.pin21, J5.pin8
  N22: J1.pin22, J2.pin22, J5.pin9
  N23: J1.pin32, J2.pin32, J4.pin18
  N24: J1.pin33, J2.pin33, J4.pin19
  N25: J1.pin34, J2.pin34, J4.pin20
  N26: J1.pin35, J2.pin35, J4.pin21
  N27: J1.pin36, J2.pin36, J4.pin22
  N28: J1.pin37, J2.pin37, J4.pin23
  N29: J1.pin38, J2.pin38, J4.pin24
  N30: J1.pin39, J2.pin39, J4.pin25
  N31: J1.pin40, J2.pin40, J4.pin26
