# Fritzing sketch Raspberry Pi_L293D_StepperMotor (saved by Fritzing 0.9.2b)
breadboards: 1

parts:
  J1 = T Cobbler Plus
  IC2 = L293D [package=THT]
  MOTOR1 = Adafruit Gear-Reduced Stepper Motor (small)

nets:
  N1: J1.5.0V#1, IC2.+Vmotor, IC2.+V
  N2: J1.GND#5, IC2.0V
  N3: J1.#4, IC2.In_1
  N4: J1.#17, IC2.In_2
  N5: J1.#23, IC2.In_4
  N6: J1.#24, IC2.In_3
  N7: IC2.Enable_1, IC2.Enable_2
  N8: IC2.Out_1_(_Controlled_by_Enable_1_), MOTOR1.PINK
  N9: IC2.Out_2_(_Controlled_by_Enable_1_), MOTOR1.ORANGE
  N10: IC2.Out_3_(_Controlled_by_Enable_2_), MOTOR1.YELLOW
  N11: IC2.Out_4_(_Controlled_by_Enable_2_), MOTOR1.BLUE

custom parts:
  T Cobbler Plus: The T-Cobbler Plus is an add on prototyping board from Adafruit specifically designed for the Raspberry Pi B+ that can break out all those tasty power, GPIO, I2C and SPI pins from the 40-pin header onto a solderless breadboard. This set will make "cobbling together" prototypes with the Pi super easy. The T-Cobbler Plus can plug into any solderless breadboard.
  Adafruit Gear-Reduced Stepper Motor (small): Adafruit gear-reduction stepper motor (small)
