# Fritzing sketch Raspberry Pi_L293D_ULN2803_StepperMotor (saved by Fritzing 0.9.2b)
breadboards: 1

parts:
  J1 = T Cobbler Plus
  VCC1 = 4 x AAA Battery Mount
  M1 = DC Motor
  IC2 = L293D [package=THT]

nets:
  N1: J1.5.0V#1, IC2.+V
  N2: J1.SCL, IC2.In_1
  N3: J1.GND#5, IC2.0V
  N4: J1.RXD, IC2.Enable_1
  N5: J1.#17, IC2.In_2
  N6: VCC1.-, VCC1.+, IC2.+Vmotor
  N7: M1.pin_1, IC2.Out_2_(_Controlled_by_Enable_1_)
  N8: M1.pin_2, IC2.Out_1_(_Controlled_by_Enable_1_)

custom parts:
  T Cobbler Plus: The T-Cobbler Plus is an add on prototyping board from Adafruit specifically designed for the Raspberry Pi B+ that can break out all those tasty power, GPIO, I2C and SPI pins from the 40-pin header onto a solderless breadboard. This set will make "cobbling together" prototypes with the Pi super easy. The T-Cobbler Plus can plug into any solderless breadboard.
