# Fritzing sketch Raspberry Pi_Servomotor (saved by Fritzing 0.9.2b)
breadboards: 1

parts:
  J1 = T Cobbler Plus
  VCC1 = 4 x AAA Battery Mount
  J2 = Basic Servo

nets:
  N1: J1.GND#8, VCC1.-, J2.gnd
  N2: J1.#18, J2.pulse
  N3: VCC1.+, J2.vcc

custom parts:
  T Cobbler Plus: The T-Cobbler Plus is an add on prototyping board from Adafruit specifically designed for the Raspberry Pi B+ that can break out all those tasty power, GPIO, I2C and SPI pins from the 40-pin header onto a solderless breadboard. This set will make "cobbling together" prototypes with the Pi super easy. The T-Cobbler Plus can plug into any solderless breadboard.
