# Fritzing sketch Raspberry Pi_ULN2803_StepperMotor (saved by Fritzing 0.9.2b)
breadboards: 1

parts:
  J1 = T Cobbler Plus
  MOTOR1 = Adafruit Gear-Reduced Stepper Motor (small)
  Q1 = ULN2803 Darlington Array

nets:
  N1: J1.5.0V#1, MOTOR1.RED, Q1.COMMON
  N2: J1.GND#5, Q1.GND
  N3: J1.#4, Q1.I1
  N4: J1.#17, Q1.I2
  N5: J1.#23, Q1.I3
  N6: J1.#24, Q1.I4
  N7: MOTOR1.ORANGE, Q1.O2
  N8: MOTOR1.YELLOW, Q1.O4
  N9: MOTOR1.PINK, Q1.O1
  N10: MOTOR1.BLUE, Q1.O3

custom parts:
  T Cobbler Plus: The T-Cobbler Plus is an add on prototyping board from Adafruit specifically designed for the Raspberry Pi B+ that can break out all those tasty power, GPIO, I2C and SPI pins from the 40-pin header onto a solderless breadboard. This set will make "cobbling together" prototypes with the Pi super easy. The T-Cobbler Plus can plug into any solderless breadboard.
  Adafruit Gear-Reduced Stepper Motor (small): Adafruit gear-reduction stepper motor (small)
  ULN2803 Darlington Array: ULN2803 Darlington Transistor Array with Flyback Protection
