# Fritzing sketch Raspberry Pi_button_led (saved by Fritzing 0.9.2b)
breadboards: 1

parts:
  S1 = Momentary Switch [package=ksa_sealed_tac_switch]
  J1 = T Cobbler Plus
  LED1 = LED - 5mm [color="Red (633nm)" package="5 mm [THT]"]
  R1 = Resistor [tolerance=±5% resistance=220 package=THT]

nets:
  N1: S1.2, J1.GND#8, R1.Pin_1
  N2: S1.4, J1.#17
  N3: J1.#18, LED1.cathode
  N4: LED1.anode, R1.Pin_0

custom parts:
  T Cobbler Plus: The T-Cobbler Plus is an add on prototyping board from Adafruit specifically designed for the Raspberry Pi B+ that can break out all those tasty power, GPIO, I2C and SPI pins from the 40-pin header onto a solderless breadboard. This set will make "cobbling together" prototypes with the Pi super easy. The T-Cobbler Plus can plug into any solderless breadboard.
