# Fritzing sketch Raspberry Pi_led_plus_rgb_led (saved by Fritzing 0.9.2b)
breadboards: 1

parts:
  J1 = T Cobbler Plus
  R1 = Resistor [tolerance=±5% resistance=270 package=THT]
  LED1 = RGB LED - (4 legs) [package="5 mm [THT]"]
  R2 = Resistor [tolerance=±5% resistance=270 package=THT]
  R3 = Resistor [tolerance=±5% resistance=270 package=THT]
  Red_LED1 = LED - 5mm [color="Red (633nm)" package="5 mm [THT]"]
  R4 = Resistor [tolerance=±5% resistance=270 package=THT]

nets:
  N1: J1.3V3, LED1.common_anode
  N2: J1.GND#8, R4.Pin_1
  N3: J1.#17, Red_LED1.anode
  N4: J1.#23, R1.Pin_0
  N5: J1.#24, R2.Pin_0
  N6: J1.#25, R3.Pin_0
  N7: R1.Pin_1, LED1.red_cathode
  N8: LED1.green_cathode, R2.Pin_1
  N9: LED1.blue_cathode, R3.Pin_1
  N10: Red_LED1.cathode, R4.Pin_0

custom parts:
  T Cobbler Plus: The T-Cobbler Plus is an add on prototyping board from Adafruit specifically designed for the Raspberry Pi B+ that can break out all those tasty power, GPIO, I2C and SPI pins from the 40-pin header onto a solderless breadboard. This set will make "cobbling together" prototypes with the Pi super easy. The T-Cobbler Plus can plug into any solderless breadboard.
