# Fritzing sketch Raspberry Pi_mcp3008_potentiometer (saved by Fritzing 0.9.2b)
breadboards: 1

parts:
  J1 = T Cobbler Plus
  IC1 = MCP3008 8-channel 10-bit ADC [part_number=MCP3008]
  POT1 = Breadboard Trimpot

nets:
  N1: J1.3V3, IC1.no_name_yet#15, IC1.no_name_yet#16, POT1.PIN3
  N2: J1.GND#5, IC1.no_name_yet#9, IC1.no_name_yet#14, POT1.PIN1
  N3: J1.#18, IC1.no_name_yet#13
  N4: J1.#23, IC1.no_name_yet#12
  N5: J1.#24, IC1.no_name_yet#11
  N6: J1.#25, IC1.no_name_yet#10
  N7: IC1.no_name_yet#1, POT1.PIN2

notes:
  channels:  0  1  2  3  4  5  6  7
  Vdd
  Vref
  AGND
  DGND

custom parts:
  T Cobbler Plus: The T-Cobbler Plus is an add on prototyping board from Adafruit specifically designed for the Raspberry Pi B+ that can break out all those tasty power, GPIO, I2C and SPI pins from the 40-pin header onto a solderless breadboard. This set will make "cobbling together" prototypes with the Pi super easy. The T-Cobbler Plus can plug into any solderless breadboard.
