# Fritzing sketch Raspberry Pi_rgb_led (saved by Fritzing 0.9.2b)
breadboards: 1

parts:
  J1 = T Cobbler Plus
  R1 = Resistor [tolerance=±5% resistance=270 package=THT]
  LED1 = RGB LED - (4 legs) [package="5 mm [THT]"]
  R2 = Resistor [tolerance=±5% resistance=270 package=THT]
  R3 = Resistor [tolerance=±5% resistance=270 package=THT]

nets:
  N1: J1.3V3, LED1.common_anode
  N2: J1.#16, R1.Pin_0
  N3: J1.#20, R2.Pin_0
  N4: J1.#21, R3.Pin_0
  N5: R1.Pin_1, LED1.red_cathode
  N6: LED1.green_cathode, R2.Pin_1
  N7: LED1.blue_cathode, R3.Pin_1

custom parts:
  T Cobbler Plus: The T-Cobbler Plus is an add on prototyping board from Adafruit specifically designed for the Raspberry Pi B+ that can break out all those tasty power, GPIO, I2C and SPI pins from the 40-pin header onto a solderless breadboard. This set will make "cobbling together" prototypes with the Pi super easy. The T-Cobbler Plus can plug into any solderless breadboard.
